# Fritzing sketch General Wiring (saved by Fritzing 0.9.3b)
circuit board: 8.46667cm x 5.64444cm
breadboards: 1

parts:
  Composant1 = Arduino Uno (Rev3)
  DRV_1 = DRV 8825 Stepper Motor Carrier, High Current [part_number="DRV 8825"]
  IC1 = Voltage Regulator [package=78xxl]
  M1 = Stepper Motor - Bipolar
  V1 = DC Power [voltage=12V]
  R1 = Resistor [tolerance=±5% resistance=220 package="2010 [SMD]"]
  U3 = 2.5mm Audio Jack [package=stereojack2.5mm_stereojack2.5mm]
  C1 = Capacitor Polarized [package=panasonic_c]
  C2 = Capacitor Polarized [package=panasonic_c]
  S1 = Pushbutton [package=THT]
  S2 = Pushbutton [package=THT]
  U4 = Optocoupler [package=THT]

nets:
  N1: Composant1.D11_PWM/MOSI, DRV_1.STEP
  N2: Composant1.D12/MISO, DRV_1.DIRECTION
  N3: Composant1.D13/SCK, R1.Pin_0
  GND: Composant1.GND, DRV_1.GROUND_ST/_MT, DRV_1.GROUND_LOG, IC1.GND, V1.V-, C1.-, C2.-, S1.leg1, S2.leg0, U4.Pin_2
  N4: Composant1.D0/RX, S1.leg0
  N5: Composant1.D1/TX, S2.leg1
  N6: Composant1.D2, DRV_1.SLEEP
  N7: Composant1.5V, IC1.OUT, C1.+
  N8: DRV_1.VOLTAGE_ST/_MT, IC1.IN, V1.V+, C2.+
  N9: DRV_1.OUT_2B, M1.A
  N10: DRV_1.OUT_2A, M1.C
  N11: DRV_1.OUT_1A, M1.B
  N12: DRV_1.OUT_1B, M1.D
  N13: R1.Pin_1, U4.Pin_1
  N14: U3.SLEEVE, U4.Pin_4
  N15: U3.LEFT, U4.Pin_5
